# Fritzing sketch Fritzing (saved by Fritzing 0.9.3b)
breadboards: 1

parts:
  R1 = Resistor [tolerance=±5% resistance=100 package=THT]
  R3 = Resistor [tolerance=±5% resistance=21 package=THT]
  LED = LTE-302 [package=lte-302]
  BC547 = TRANSISTOR_NPN_2 [package=to-92]
  part = Adafruit HUZZAH ESP8266 Breakout [part_number=2471]

nets:
  N1: R1.Pin_0, part.V+
  N2: R1.Pin_1, BC547.C
  N3: R3.Pin_0, part.#5
  N4: R3.Pin_1, BC547.B
  N5: LED.A, BC547.E
  N6: LED.C, part.GND
